# Fritzing sketch brightness (saved by Fritzing 0.9.2b)
breadboards: 1

parts:
  U1 = NodeMCU V1.0
  LED1 = LED - 5mm [color="Red (633nm)" package="5 mm [THT]"]
  R1 = Resistor [tolerance=±5% resistance=330 package=THT]
  R2 = Photocell (LDR) [package=THT]
  R3 = Resistor [tolerance=±5% resistance=10k package=THT]

nets:
  N1: U1.D3, R1.Pin_1
  N2: U1.GND, LED1.cathode, R3.Pin_0
  N3: U1.A0, R2.pin_1
  N4: LED1.anode, R1.Pin_0
  N5: R2.pin_0, R3.Pin_1

custom parts:
  NodeMCU V1.0: ESP8266 based NodeMCU
