# Fritzing sketch indicator (saved by Fritzing 0.9.2b)
breadboards: 2

parts:
  U1 = NodeMCU V1.0
  U2 = 7-SEGMENT-DISPLAY-1_-RED [package=7-segment-1_pth]

nets:
  N1: U1.D0, U2.A
  N2: U1.D1, U2.B
  N3: U1.D2, U2.C
  N4: U1.D3, U2.D
  N5: U1.GND, U2.G1, U2.G2
  N6: U1.D5, U2.E
  N7: U1.D6, U2.F
  N8: U1.D7, U2.G

custom parts:
  NodeMCU V1.0: ESP8266 based NodeMCU
